// Logisim project Circuito Demultiplexador - ok.circ as structural Verilog: 2 circuits, main circuit main
module main (
  input  S2,
  input  S1,
  input  S0,
  input  ENTRADA,
  output B0,
  output B1,
  output B2,
  output B3,
  output B4,
  output B5,
  output B6,
  output B7
);

  wire not_1_out, not_2_out, not_3_out;

  not not_1 (not_1_out, S2);
  not not_2 (not_2_out, S1);
  not not_3 (not_3_out, S0);
  and _0 (B0, not_1_out, not_2_out, not_3_out, ENTRADA);
  and _1 (B1, not_1_out, not_2_out, S0, ENTRADA);
  and _2 (B2, not_1_out, S1, not_3_out, ENTRADA);
  and _3 (B3, not_1_out, S1, S0, ENTRADA);
  and _4 (B4, S2, not_2_out, not_3_out, ENTRADA);
  and _5 (B5, S2, not_2_out, S0, ENTRADA);
  and _6 (B6, S1, S2, not_3_out, ENTRADA);
  and _7 (B7, S1, S2, S0, ENTRADA);

  // Notes on the sheet:
  //   SAIDAS
endmodule

module MAIORIA (
  input  A,
  input  B,
  input  B_2,
  output out_4
);

  wire and_1_out, and_2_out, and_3_out, not_1_out, not_2_out, not_3_out;

  not not_1 (not_1_out, A);
  not not_2 (not_2_out, B);
  not not_3 (not_3_out, B_2);
  and and_1 (and_1_out, not_1_out, B, B_2);
  and and_2 (and_2_out, A, not_2_out, B_2);
  or or_1 (out_4, and_1_out, and_2_out, and_3_out);
  and and_3 (and_3_out, A, B, B_2);

  // Notes on the sheet:
  //   FUNÇÃO MAIORIA
  //   M = f(A, B, C)
endmodule
