// Logisim project Circuito Função Maioria - ok.circ as structural Verilog: 2 circuits, main circuit main
module main (
  input  A,
  input  B,
  input  C,
  output out_4
);

  wire and_1_out, and_2_out, and_3_out, and_4_out, not_1_out, not_2_out, not_3_out;

  not not_1 (not_1_out, A);
  not not_2 (not_2_out, B);
  not not_3 (not_3_out, C);
  and and_1 (and_1_out, not_1_out, B, C);
  and and_2 (and_2_out, A, not_2_out, C);
  or or_1 (out_4, and_1_out, and_2_out, and_3_out, and_4_out);
  and and_3 (and_3_out, A, B, not_3_out);
  and and_4 (and_4_out, A, B, C);
endmodule

module MAIORIA (
  input  A,
  input  B,
  input  B_2,
  output out_4
);

  wire and_1_out, and_2_out, and_3_out, not_1_out, not_2_out, not_3_out;

  not not_1 (not_1_out, A);
  not not_2 (not_2_out, B);
  not not_3 (not_3_out, B_2);
  and and_1 (and_1_out, not_1_out, B, B_2);
  and and_2 (and_2_out, A, not_2_out, B_2);
  or or_1 (out_4, and_1_out, and_2_out, and_3_out);
  and and_3 (and_3_out, A, B, B_2);

  // Notes on the sheet:
  //   FUNÇÃO MAIORIA
  //   M = f(A, B, C)
endmodule
