// Logisim project Circuito Meio Somador - ok.circ as structural Verilog: 1 circuit, main circuit main
module main (
  input  A,
  input  B,
  output RESULTADO,
  output V1
);

  xnor xnor_1 (RESULTADO, A, B);
  and and_1 (V1, A, B);

  // Notes on the sheet:
  //   vai 0
  //   0
  //   +
  //   0
  //   0
  //   vai 0
  //   0
  //   +
  //   +
  //   1
  //   1
  //   vai 1
  //   vai 0
  //   1
  //   1
  //   +
  //   1
  //   0
  //   0
  //   1
  //   CIRCUITO MEIO SOMADOR
endmodule
