// Logisim project Circuito Multiplexador - ok.circ as structural Verilog
module main (
  input  C0,
  input  C1,
  input  C2,
  input  in_4,
  output S
);

  wire _1_out, _2_out, _3_out, _4_out, _5_out, _6_out, _7_out, _8_out, not_1_out, not_2_out, not_3_out;

  not not_1 (not_1_out, C0);
  not not_2 (not_2_out, C1);
  not not_3 (not_3_out, C2);
  and _1 (_1_out, in_4, not_1_out, not_2_out, not_3_out);
  and _2 (_2_out, in_4, not_1_out, not_2_out, C2);
  and _3 (_3_out, in_4, not_1_out, C1, not_3_out);
  and _4 (_4_out, in_4, not_1_out, C1, C2);
  and _5 (_5_out, in_4, C0, not_2_out, not_3_out);
  and _6 (_6_out, in_4, C0, not_2_out, C2);
  and _7 (_7_out, in_4, C0, C1, not_3_out);
  and _8 (_8_out, in_4, C0, not_2_out, not_3_out);
  or or_1 (S, _1_out, _2_out, _3_out, _4_out, _5_out, _6_out, _7_out, _8_out);

  // Notes on the sheet:
  //   E0
  //   E1
  //   E2
  //   E3
  //   E4
  //   E5
  //   E6
  //   E7
endmodule
