// Logisim project Circuito Somador Completo - ok.circ as structural Verilog: 1 circuit, main circuit main
module main (
  input  CIN,
  input  A,
  input  B,
  output RESULTADO,
  output COUT
);

  wire and_1_out, and_2_out, xor_1_out;

  and and_1 (and_1_out, B, A);
  xor xor_1 (xor_1_out, A, B);
  xor xor_2 (RESULTADO, CIN, xor_1_out);
  and and_2 (and_2_out, CIN, xor_1_out);
  or or_1 (COUT, and_2_out, and_1_out);

  // Notes on the sheet:
  //   CIRCUITO SOMADOR COMPLETO
endmodule
