// Logisim project Circuitos Universalidades da Portas - ok.circ as structural Verilog: 1 circuit, main circuit main
module main (
  input  A,
  input  A_2,
  input  AB,
  input  B,
  input  B_2,
  input  A_3,
  input  A_4,
  input  B_3,
  input  B_4,
  input  B_5,
  input  B_6,
  output out_12,
  output A___B,
  output A___B_2,
  output B_tilde,
  output B_tilde_2
);

  wire nand_1_out, nand_2_out, nand_3_out, nand_5_out, nor_1_out, nor_2_out, nor_3_out;

  nor nor_1 (nor_1_out, A_4, B_3);
  nor nor_2 (nor_2_out, A, A);
  nor nor_3 (nor_3_out, B_2, B_2);
  nor nor_4 (B_tilde, B_5, B_5);
  nor nor_5 (out_12, nor_2_out, nor_3_out);
  nor nor_6 (A___B, nor_1_out, nor_1_out);
  nand nand_1 (nand_1_out, A_2, B);
  nand nand_2 (nand_2_out, A_3, A_3);
  nand nand_3 (nand_3_out, B_4, B_4);
  nand nand_4 (B_tilde_2, B_6, B_6);
  nand nand_5 (nand_5_out, nand_1_out, nand_1_out);
  nand nand_6 (A___B_2, nand_2_out, nand_3_out);

  // Notes on the sheet:
  //   (A + B)~ = A~ * B~
  //   NOR
  //   NOR
  //   NOR
  //   (B + B)~ = B~* B~ = B~ 
  //   AND
  //   A~
  //   B~
  //   OR
  //   NOT
  //   (A~ * B~) = A  B
  //   ((A~B~) +  (A~B~))~ = (A + B) * (A + B) = A + B
  //   A B
  //   (A*B)~ = A~ + B~
  //   NAND
  //   AND
  //   NAND
  //   OR
  //   A~
  //   B~
  //   NOT
  //   NAND
  //   (B + B)~ = B~* B~ = B~ 
  //   ((A~+B~) *  (A~+B~))~ = AB + AB = AB
  //   (A~ + B~)~ = A * B
endmodule
