// Logisim project ULA 1 Bit - ok(verificar).circ as structural Verilog: 1 circuit, main circuit main
module main (
  input  VEM__UM,
  input  A,
  input  in_3,
  input  in_4,
  input  B,
  input  in_6,
  input  E0,
  input  E1,
  input  VAI__UM,
  output \SAÍDA 
);

  wire and_1_out, and_2_out, and_3_out, and_4_out, and_5_out, and_6_out, and_7_out, and_8_out, and_9_out,
       and_10_out, and_11_out, and_12_out, and_13_out, not_1_out, not_2_out, not_3_out, not_4_out, not_5_out,
       or_1_out, xor_1_out, xor_2_out, xor_3_out;

  and and_1 (and_1_out, in_3, in_4);
  and and_2 (and_2_out, B, in_6);
  not not_1 (not_1_out, E0);
  not not_2 (not_2_out, E1);
  not not_3 (not_3_out, E0);
  not not_4 (not_4_out, E1);
  xor xor_1 (xor_1_out, A, and_1_out);
  and and_3 (and_3_out, xor_1_out, and_2_out);
  or or_1 (or_1_out, xor_1_out, and_2_out);
  not not_5 (not_5_out, and_2_out);
  and and_4 (and_4_out, not_1_out, not_2_out);
  and and_5 (and_5_out, not_3_out, E1);
  and and_6 (and_6_out, E0, not_4_out);
  and and_7 (and_7_out, E0, E1);
  and and_8 (and_8_out, and_3_out, and_4_out);
  and and_9 (and_9_out, or_1_out, and_5_out);
  and and_10 (and_10_out, not_5_out, and_6_out);
  and and_11 (and_11_out, and_7_out, xor_1_out, and_2_out);
  or or_2 (VAI__UM, and_11_out, and_12_out);
  xor xor_2 (xor_2_out, and_2_out, xor_1_out);
  and and_12 (and_12_out, and_7_out, xor_2_out, VEM__UM);
  xor xor_3 (xor_3_out, VEM__UM, xor_2_out);
  and and_13 (and_13_out, xor_3_out, and_7_out);
  or or_3 (\SAÍDA , and_8_out, and_9_out, and_10_out, and_13_out);
endmodule
