// Logisim project ULA 32 Bit.circ as structural Verilog: 3 circuits, main circuit main
module main (
  input  VEM__UM,
  input  A,
  input  in_3,
  input  in_4,
  input  B,
  input  in_6,
  input  E0,
  input  E1,
  input  VAI__UM,
  output \SAÍDA 
);

  wire and_1_out, and_2_out, and_3_out, and_4_out, and_5_out, and_6_out, and_7_out, and_8_out, and_9_out,
       and_10_out, and_11_out, and_12_out, and_13_out, not_1_out, not_2_out, not_3_out, not_4_out, not_5_out,
       or_1_out, xor_1_out, xor_2_out, xor_3_out;

  and and_1 (and_1_out, in_3, in_4);
  and and_2 (and_2_out, B, in_6);
  not not_1 (not_1_out, E0);
  not not_2 (not_2_out, E1);
  not not_3 (not_3_out, E0);
  not not_4 (not_4_out, E1);
  xor xor_1 (xor_1_out, A, and_1_out);
  and and_3 (and_3_out, xor_1_out, and_2_out);
  or or_1 (or_1_out, xor_1_out, and_2_out);
  not not_5 (not_5_out, and_2_out);
  and and_4 (and_4_out, not_1_out, not_2_out);
  and and_5 (and_5_out, not_3_out, E1);
  and and_6 (and_6_out, E0, not_4_out);
  and and_7 (and_7_out, E0, E1);
  and and_8 (and_8_out, and_3_out, and_4_out);
  and and_9 (and_9_out, or_1_out, and_5_out);
  and and_10 (and_10_out, not_5_out, and_6_out);
  and and_11 (and_11_out, and_7_out, xor_1_out, and_2_out);
  or or_2 (VAI__UM, and_11_out, and_12_out);
  xor xor_2 (xor_2_out, and_2_out, xor_1_out);
  and and_12 (and_12_out, and_7_out, xor_2_out, VEM__UM);
  xor xor_3 (xor_3_out, VEM__UM, xor_2_out);
  and and_13 (and_13_out, xor_3_out, and_7_out);
  or or_3 (\SAÍDA , and_8_out, and_9_out, and_10_out, and_13_out);
endmodule

module ula_1_bit (
  input  SUB,
  input  CIN,
  input  [2:0] in_3,
  input  A,
  input  B,
  input  LESS,
  output \SAÍDA ,
  output COUT,
  output SET
);

  wire and_1_out, nor_1_out, or_1_out, xor_1_out, xor_2_out;

  xor xor_1 (xor_1_out, B, SUB);
  and and_1 (and_1_out, A, B);
  or or_1 (or_1_out, A, B);
  xor xor_2 (xor_2_out, A, B);
  nor nor_1 (nor_1_out, A, B);
  Adder #(.width(1)) adder_1 (.a(A), .b(xor_1_out), .out(SET), .cin(CIN), .cout(COUT));
  Multiplexer #(.select(3), .enable("false")) multiplexer_1 (
    .in0(and_1_out), .in1(or_1_out), .in2(xor_2_out), .in3(nor_1_out), .in4(SET), .in5(LESS), .out(\SAÍDA ),
    .sel(in_3));  // open: in6, in7
endmodule

module ULA_32BITS (
  input  [2:0] OP,
  input  in_2,
  input  [31:0] A,
  input  [31:0] B,
  output [31:0] RESULTADO
);

  wire ula_1_bit_1_cout, ula_1_bit_2_cout, ula_1_bit_3_cout, ula_1_bit_4_cout, ula_1_bit_5_cout,
       ula_1_bit_6_cout, ula_1_bit_7_cout, ula_1_bit_8_cout, ula_1_bit_10_cout, ula_1_bit_11_cout,
       ula_1_bit_12_cout, ula_1_bit_13_cout, ula_1_bit_14_cout, ula_1_bit_15_cout, ula_1_bit_16_cout,
       ula_1_bit_17_cout, ula_1_bit_18_cout, ula_1_bit_19_cout, ula_1_bit_20_cout, ula_1_bit_21_cout,
       ula_1_bit_22_cout, ula_1_bit_23_cout, ula_1_bit_24_cout, ula_1_bit_25_cout, ula_1_bit_26_cout,
       ula_1_bit_27_cout, ula_1_bit_28_cout, ula_1_bit_29_cout, ula_1_bit_30_cout, ula_1_bit_31_cout,
       ula_1_bit_32_set;

  ula_1_bit ula_1_bit_1 (
    .A(A[0]), .B(B[0]), .LESS(ula_1_bit_32_set), .\SAÍDA (RESULTADO[0]), .SUB(A[16]), .CIN(A[16]), .in_3(OP),
    .COUT(ula_1_bit_1_cout));  // open: SET
  ula_1_bit ula_1_bit_2 (
    .A(A[1]), .B(B[1]), .LESS(1'b0), .\SAÍDA (RESULTADO[1]), .SUB(A[16]), .CIN(ula_1_bit_1_cout), .in_3(OP),
    .COUT(ula_1_bit_2_cout));  // open: SET
  ula_1_bit ula_1_bit_3 (
    .A(A[3]), .B(B[3]), .LESS(1'b0), .\SAÍDA (RESULTADO[3]), .SUB(A[16]), .CIN(ula_1_bit_16_cout), .in_3(OP),
    .COUT(ula_1_bit_3_cout));  // open: SET
  ula_1_bit ula_1_bit_4 (
    .A(A[4]), .B(B[4]), .LESS(1'b0), .\SAÍDA (RESULTADO[4]), .SUB(A[16]), .CIN(ula_1_bit_3_cout), .in_3(OP),
    .COUT(ula_1_bit_4_cout));  // open: SET
  ula_1_bit ula_1_bit_5 (
    .A(A[5]), .B(B[5]), .LESS(1'b0), .\SAÍDA (RESULTADO[5]), .SUB(A[16]), .CIN(ula_1_bit_4_cout), .in_3(OP),
    .COUT(ula_1_bit_5_cout));  // open: SET
  ula_1_bit ula_1_bit_6 (
    .A(A[6]), .B(B[6]), .LESS(1'b0), .\SAÍDA (RESULTADO[6]), .SUB(A[16]), .CIN(ula_1_bit_5_cout), .in_3(OP),
    .COUT(ula_1_bit_6_cout));  // open: SET
  ula_1_bit ula_1_bit_7 (
    .A(A[7]), .B(B[7]), .LESS(1'b0), .\SAÍDA (RESULTADO[7]), .SUB(A[16]), .CIN(ula_1_bit_6_cout), .in_3(OP),
    .COUT(ula_1_bit_7_cout));  // open: SET
  ula_1_bit ula_1_bit_8 (
    .A(A[8]), .B(B[29]), .LESS(1'b0), .\SAÍDA (RESULTADO[8]), .SUB(A[16]), .CIN(ula_1_bit_7_cout), .in_3(OP),
    .COUT(ula_1_bit_8_cout));  // open: SET
  ula_1_bit ula_1_bit_9 (
    .A(A[9]), .B(B[8]), .LESS(1'b0), .\SAÍDA (RESULTADO[9]), .SUB(A[16]), .CIN(ula_1_bit_8_cout), .in_3(OP));  // open: COUT, SET
  ula_1_bit ula_1_bit_10 (
    .A(A[10]), .B(B[9]), .LESS(1'b0), .\SAÍDA (RESULTADO[10]), .SUB(A[16]), .in_3(OP),
    .COUT(ula_1_bit_10_cout));  // open: CIN, SET
  ula_1_bit ula_1_bit_11 (
    .A(A[11]), .B(B[30]), .LESS(1'b0), .\SAÍDA (RESULTADO[11]), .SUB(A[16]), .CIN(ula_1_bit_10_cout),
    .in_3(OP), .COUT(ula_1_bit_11_cout));  // open: SET
  ula_1_bit ula_1_bit_12 (
    .A(A[12]), .B(B[31]), .\SAÍDA (RESULTADO[12]), .SUB(A[16]), .CIN(ula_1_bit_11_cout), .in_3(OP),
    .COUT(ula_1_bit_12_cout));  // open: LESS, SET
  ula_1_bit ula_1_bit_13 (
    .A(A[13]), .B(B[10]), .LESS(1'b0), .\SAÍDA (RESULTADO[13]), .SUB(A[16]), .CIN(ula_1_bit_12_cout),
    .in_3(OP), .COUT(ula_1_bit_13_cout));  // open: SET
  ula_1_bit ula_1_bit_14 (
    .A(A[14]), .B(B[11]), .LESS(1'b0), .\SAÍDA (RESULTADO[14]), .SUB(A[16]), .CIN(ula_1_bit_13_cout),
    .in_3(OP), .COUT(ula_1_bit_14_cout));  // open: SET
  ula_1_bit ula_1_bit_15 (
    .A(A[15]), .B(B[12]), .LESS(1'b0), .\SAÍDA (RESULTADO[15]), .SUB(A[16]), .CIN(ula_1_bit_14_cout),
    .in_3(OP), .COUT(ula_1_bit_15_cout));  // open: SET
  ula_1_bit ula_1_bit_16 (
    .A(A[2]), .B(B[2]), .LESS(1'b0), .\SAÍDA (RESULTADO[2]), .SUB(A[16]), .CIN(ula_1_bit_2_cout), .in_3(OP),
    .COUT(ula_1_bit_16_cout));  // open: SET
  ula_1_bit ula_1_bit_17 (
    .A(A[16]), .B(B[13]), .LESS(1'b0), .\SAÍDA (RESULTADO[16]), .SUB(A[16]), .CIN(ula_1_bit_15_cout),
    .in_3(OP), .COUT(ula_1_bit_17_cout));  // open: SET
  ula_1_bit ula_1_bit_18 (
    .A(A[17]), .B(B[14]), .LESS(1'b0), .\SAÍDA (RESULTADO[17]), .SUB(A[16]), .CIN(ula_1_bit_17_cout),
    .in_3(OP), .COUT(ula_1_bit_18_cout));  // open: SET
  ula_1_bit ula_1_bit_19 (
    .A(A[18]), .B(B[15]), .LESS(1'b0), .\SAÍDA (RESULTADO[18]), .SUB(A[16]), .CIN(ula_1_bit_18_cout),
    .in_3(OP), .COUT(ula_1_bit_19_cout));  // open: SET
  ula_1_bit ula_1_bit_20 (
    .A(A[19]), .B(B[16]), .LESS(1'b0), .\SAÍDA (RESULTADO[19]), .SUB(A[16]), .CIN(ula_1_bit_19_cout),
    .in_3(OP), .COUT(ula_1_bit_20_cout));  // open: SET
  ula_1_bit ula_1_bit_21 (
    .A(A[20]), .B(B[17]), .LESS(1'b0), .\SAÍDA (RESULTADO[20]), .SUB(A[16]), .CIN(ula_1_bit_20_cout),
    .in_3(OP), .COUT(ula_1_bit_21_cout));  // open: SET
  ula_1_bit ula_1_bit_22 (
    .A(A[21]), .B(B[18]), .LESS(1'b0), .\SAÍDA (RESULTADO[21]), .SUB(A[16]), .CIN(ula_1_bit_21_cout),
    .in_3(OP), .COUT(ula_1_bit_22_cout));  // open: SET
  ula_1_bit ula_1_bit_23 (
    .A(A[22]), .B(B[19]), .LESS(1'b0), .\SAÍDA (RESULTADO[22]), .SUB(A[16]), .CIN(ula_1_bit_22_cout),
    .in_3(OP), .COUT(ula_1_bit_23_cout));  // open: SET
  ula_1_bit ula_1_bit_24 (
    .A(A[23]), .B(B[20]), .LESS(1'b0), .\SAÍDA (RESULTADO[23]), .SUB(A[16]), .CIN(ula_1_bit_23_cout),
    .in_3(OP), .COUT(ula_1_bit_24_cout));  // open: SET
  ula_1_bit ula_1_bit_25 (
    .A(A[24]), .B(B[21]), .LESS(1'b0), .\SAÍDA (RESULTADO[24]), .SUB(A[16]), .CIN(ula_1_bit_24_cout),
    .in_3(OP), .COUT(ula_1_bit_25_cout));  // open: SET
  ula_1_bit ula_1_bit_26 (
    .A(A[25]), .B(B[22]), .LESS(1'b0), .\SAÍDA (RESULTADO[25]), .SUB(A[16]), .CIN(ula_1_bit_25_cout),
    .in_3(OP), .COUT(ula_1_bit_26_cout));  // open: SET
  ula_1_bit ula_1_bit_27 (
    .A(A[26]), .B(B[23]), .LESS(1'b0), .\SAÍDA (RESULTADO[26]), .SUB(A[16]), .CIN(ula_1_bit_26_cout),
    .in_3(OP), .COUT(ula_1_bit_27_cout));  // open: SET
  ula_1_bit ula_1_bit_28 (
    .A(A[27]), .B(B[24]), .LESS(1'b0), .\SAÍDA (RESULTADO[27]), .SUB(A[16]), .CIN(ula_1_bit_27_cout),
    .in_3(OP), .COUT(ula_1_bit_28_cout));  // open: SET
  ula_1_bit ula_1_bit_29 (
    .A(A[28]), .B(B[25]), .LESS(1'b0), .\SAÍDA (RESULTADO[28]), .SUB(A[16]), .CIN(ula_1_bit_28_cout),
    .in_3(OP), .COUT(ula_1_bit_29_cout));  // open: SET
  ula_1_bit ula_1_bit_30 (
    .A(A[29]), .B(B[26]), .LESS(1'b0), .\SAÍDA (RESULTADO[29]), .SUB(A[16]), .CIN(ula_1_bit_29_cout),
    .in_3(OP), .COUT(ula_1_bit_30_cout));  // open: SET
  ula_1_bit ula_1_bit_31 (
    .A(A[30]), .B(B[27]), .LESS(1'b0), .\SAÍDA (RESULTADO[30]), .SUB(A[16]), .CIN(ula_1_bit_30_cout),
    .in_3(OP), .COUT(ula_1_bit_31_cout));  // open: SET
  ula_1_bit ula_1_bit_32 (
    .A(A[31]), .B(B[28]), .LESS(1'b0), .\SAÍDA (RESULTADO[31]), .SUB(A[16]), .CIN(ula_1_bit_31_cout),
    .in_3(OP), .SET(ula_1_bit_32_set));  // open: COUT

  assign in_2 = A[16];
endmodule
